# Fritzing sketch DroidOS (saved by Fritzing 0.9.3b)
circuit board: 8.21917cm x 4.06295cm
breadboards: 1

parts:
  Teensy_3_1 = Teensy 3.1
  Audio = 3.5mm Audio Jack [package=audio-jack]
  + = Pad [width=7.3247042000434464 height=4.1925462585954119 connect=center]
  5V_REG = female pin header, 3 pins [form="♀ (female)"]
  SBUS/PPM = female pin header, 3 pins [form="♀ (female)"]
  SBUS_INV = female pin header, 3 pins [form="♀ (female)"]
  PWM_OUT_2 = female pin header, 3 pins [form="♀ (female)"]
  PWM_OUT_1 = female pin header, 3 pins [form="♀ (female)"]
  PWM_OUT_4 = female pin header, 3 pins [form="♀ (female)"]
  PWM_OUT_3 = female pin header, 3 pins [form="♀ (female)"]
  - = Pad [width=7.3247042000434464 height=4.1925462585954119 connect=center]  # not connected
  Q1 = NPN-Transistor [package="SOT-23 [SMD]"]
  R1 = 220 Ω Resistor [tolerance=±5% package="0805 [SMD]"]
  R2 = 220 Ω Resistor [tolerance=±5% package="0805 [SMD]"]
  J2 = female pin header, 3 pins [form="♀ (female)"]
  J3 = female pin header, 8 pins [form="♀ (female)"]
  J4 = female pin header, 8 pins [form="♀ (female)"]
  SPK = female pin header, 3 pins [form="♀ (female)"]
  DFPlayer_Mini = DFRobot DFPlayer Mini [part_number=DFR0299]

nets:
  N1: Teensy_3_1.GND, J3.pin1
  N2: Teensy_3_1.D0, J3.pin2
  N3: Teensy_3_1.D1, J3.pin3
  N4: Teensy_3_1.D2, J3.pin4
  N5: Teensy_3_1.D3, J3.pin5
  N6: Teensy_3_1.D4, J3.pin6
  N7: Teensy_3_1.D5, J3.pin7
  N8: Teensy_3_1.D6, J3.pin8
  N9: Teensy_3_1.D7, J2.pin2
  N10: Teensy_3_1.D9, DFPlayer_Mini.TX
  N11: Teensy_3_1.D10, DFPlayer_Mini.RX
  N12: Teensy_3_1.A2/D16, PWM_OUT_4.pin3
  N13: Teensy_3_1.A6/D20, PWM_OUT_3.pin3
  N14: Teensy_3_1.A8/D22, PWM_OUT_2.pin3
  N15: Teensy_3_1.A9/D23, PWM_OUT_1.pin3
  3V3: Teensy_3_1.3V3, DFPlayer_Mini.VCC
  N16: Teensy_3_1.Vin, 5V_REG.pin3, PWM_OUT_2.pin2, PWM_OUT_1.pin2, PWM_OUT_4.pin2, PWM_OUT_3.pin2
  N17: Audio.RIGHT, DFPlayer_Mini.DAC_R
  N18: Audio.LEFT, DFPlayer_Mini.DAC_L
  N19: +.pad, 5V_REG.pin1
  N20: SBUS/PPM.pin3, J2.pin1
  N21: SBUS_INV.pin3, Q1.0, R1.Pin_0, R1.GND, R2.Pin_0
  N22: Q1.1, J2.pin3
  N23: J4.pin1, DFPlayer_Mini.BUSY
  N24: J4.pin2, DFPlayer_Mini.USB_NEG
  N25: J4.pin3, DFPlayer_Mini.USB_POS
  N26: J4.pin4, DFPlayer_Mini.ADKEY_2
  N27: J4.pin5, DFPlayer_Mini.ADKEY_1
  N28: J4.pin6, DFPlayer_Mini.IO_2
  N29: J4.pin7, DFPlayer_Mini.GND-1, DFPlayer_Mini.GND-2
  N30: J4.pin8, DFPlayer_Mini.IO_1
  N31: SPK.pin1, DFPlayer_Mini.SPK_1
  N32: SPK.pin3, DFPlayer_Mini.SPK_2

notes:
  NORM
  INV
  DroidOS
  v0.2 rev A
  By Joey Gennari
  Teensy LC
  1S - 4S

custom parts:
  220 Ω Resistor: A generic resistor
